// Logisim project main.circ as structural Verilog: 1 circuit, main circuit main
module main (
);

  wire A_READ, A_WRITE, adder_1_cout, ALU_READ, ALU_WRITE, and_1_out, and_2_out, and_4_out, and_5_out,
       and_6_out, and_7_out, and_10_out, and_11_out, B_READ, B_WRITE, button_1_out, C_READ, C_WRITE, CARRY,
       CLK, decoder_1_out0, decoder_1_out1, decoder_1_out2, decoder_1_out3, IN_READ, IR_WRITE, MAR_READ,
       MAR_WRITE, not_1_out, not_2_out, not_3_out, or_6_out, OUT_WRITE, PC_COUNT, PC_READ, PC_READ_A,
       PC_READ_C, PC_WRITE, PC_WRITE_A, RAM_ADDR_SEL, RAM_READ, RAM_WRITE, READ_EN, RESET, SEG_SEL,
       SEG_WRITE, subtractor_1_bout, ZERO;
  wire [0:0] ALU_q_2;
  wire [1:0] nor_1_out;
  wire [4:0] SEG_ADDR, SEGC_q, SEGD_q;
  wire [6:0] keyboard_1_data, pull_resistor_2_node, ram_1_data;
  wire [7:0] A_q, adder_1_out, ALU_q, B_q, C_q, MAR, multiplexer_2_out, multiplexer_3_out, multiplexer_4_out,
       nand_1_out, PC_q, shifter_1_out, subtractor_1_out;
  wire [7:6] IR_q;
  wire [7:7] keyboard_1_avail, ram_1_data_2;
  wire [12:0] multiplexer_1_out;

  Clock clock_1 (.out(CLK));
  Button button_1 (.out(button_1_out));
  Register #(.width(5)) SEGC (.D(SEG_ADDR), .en(and_1_out), .clk(not_1_out), .Q(SEGC_q), .clr(RESET));
  and and_1 (and_1_out, SEG_WRITE, ~SEG_SEL);  // AND_Gate
  not not_1 (not_1_out, CLK);
  Register u_MAR (.D({ram_1_data_2[7], ram_1_data}), .en(MAR_WRITE), .clk(CLK), .Q(MAR));  // open: clr
  Register #(.width(5)) SEGD (.D(SEG_ADDR), .en(and_2_out), .clk(not_2_out), .Q(SEGD_q), .clr(RESET));
  and and_2 (and_2_out, SEG_WRITE, SEG_SEL);
  not not_2 (not_2_out, CLK);
  and and_3 (RESET, CLK, button_1_out);
  Counter PC (
    .load(PC_WRITE), .D({ram_1_data_2[7], ram_1_data}), .count(PC_COUNT), .Q(PC_q), .clk(CLK), .clr(RESET));  // open: carry, up
  Multiplexer #(.enable("false"), .width(13)) multiplexer_1 (
    .in0({SEGC_q, PC_q}), .in1({SEGD_q, MAR}), .out(multiplexer_1_out), .sel(RAM_ADDR_SEL));
  TTY tty_1 (.data(ram_1_data), .clk(CLK), .we(OUT_WRITE), .clr(RESET));
  RAM #(.addrWidth(13), .databus("bidir"), .readbehav("war"), .trigger("falling"), .\type ("nonvolatile")) ram_1 (
    .addr(multiplexer_1_out), .we(RAM_WRITE), .oe(RAM_READ), .clk(CLK), .data({ram_1_data_2[7], ram_1_data}));
  and and_4 (and_4_out, OUT_WRITE, ram_1_data_2[7]);
  Keyboard keyboard_1 (.clk(and_4_out), .clr(RESET), .avail(keyboard_1_avail[7]), .data(keyboard_1_data));  // open: re
  or or_1 (RAM_ADDR_SEL, RAM_WRITE, MAR_READ);
  or or_2 (RAM_READ, PC_READ, MAR_READ);
  or or_3 (PC_READ, PC_READ_A, IR_WRITE, PC_READ_C);
  or or_4 (PC_WRITE, PC_WRITE_A, PC_READ_C);
  D_Flip_Flop d_ff_1 (.D(READ_EN), .clk(CLK), .Q(IR_WRITE), .Qn(READ_EN), .preset(RESET));  // open: reset
  and and_5 (and_5_out, READ_EN, PC_READ);
  assign {ram_1_data_2[7], ram_1_data} = IN_READ ? {keyboard_1_avail[7], keyboard_1_data} : 8'bz;  // Controlled_Buffer controlled_buffer_1
  // Probe on {ram_1_data_2[7], ram_1_data}
  Register IR (
    .D({ram_1_data_2[7], ram_1_data}), .en(IR_WRITE), .clk(CLK), .Q({IR_q, SEG_SEL, SEG_ADDR}));  // open: clr
  Pull_Resistor pull_resistor_1 (.node({ram_1_data_2[7], ram_1_data}));
  or or_5 (PC_COUNT, IR_WRITE, and_5_out);
  Register A (.D({ram_1_data_2[7], ram_1_data}), .en(A_WRITE), .clk(CLK), .Q(A_q));  // open: clr
  Register B (.D({ram_1_data_2[7], ram_1_data}), .en(B_WRITE), .clk(CLK), .Q(B_q));  // open: clr
  Register C (.D({ram_1_data_2[7], ram_1_data}), .en(C_WRITE), .clk(CLK), .Q(C_q));  // open: clr
  Register ALU (
    .D({ram_1_data_2[7], ram_1_data}), .en(ALU_WRITE), .clk(CLK), .Q({ALU_q[7], ALU_q_2[0], ALU_q[5:0]}));  // open: clr
  assign {ram_1_data_2[7], ram_1_data} = A_READ ? A_q : 8'bz;  // Controlled_Buffer controlled_buffer_2
  assign {ram_1_data_2[7], ram_1_data} = B_READ ? B_q : 8'bz;  // Controlled_Buffer controlled_buffer_3
  assign {ram_1_data_2[7], ram_1_data} = C_READ ? C_q : 8'bz;  // Controlled_Buffer controlled_buffer_4
  // Probe on {SEG_SEL, SEG_ADDR[4:3]}
  Decoder #(.enable("false"), .select(2)) decoder_1 (
    .out0(decoder_1_out0), .out1(decoder_1_out1), .out2(decoder_1_out2), .out3(decoder_1_out3), .sel(IR_q));
  Pull_Resistor pull_resistor_2 (.node(pull_resistor_2_node));
  // Probe on ALU_q[5:4]
  // Probe on SEG_ADDR[2:0]
  Multiplexer #(.enable("false"), .select(2), .width(8)) multiplexer_2 (
    .in0(A_q), .in1(B_q), .in2(C_q), .in3(MAR), .out(multiplexer_2_out), .sel(ALU_q[3:2]));
  // Probe on ALU_q[3:2]
  Multiplexer #(.enable("false"), .select(2), .width(8)) multiplexer_3 (
    .in0(A_q), .in1(B_q), .in2(C_q), .in3({pull_resistor_2_node, ALU_q_2[0]}), .out(multiplexer_3_out),
    .sel(ALU_q[5:4]));
  not not_3 (not_3_out, decoder_1_out3);
  or or_6 (or_6_out, decoder_1_out0, and_6_out, and_7_out);
  and and_6 (and_6_out, decoder_1_out1, ZERO);
  and and_7 (and_7_out, decoder_1_out2, CARRY);
  and and_8 (SEG_WRITE, READ_EN, decoder_1_out3);
  and and_9 (PC_READ_C, SEG_WRITE, ~SEG_SEL);  // AND_Gate
  // Probe on multiplexer_4_out
  assign {ram_1_data_2[7], ram_1_data} = ALU_READ ? multiplexer_4_out : 8'bz;  // Controlled_Buffer controlled_buffer_5
  Adder adder_1 (.a(multiplexer_2_out), .b(multiplexer_3_out), .out(adder_1_out), .cin(ALU_q[7]), .cout(adder_1_cout));
  Subtractor subtractor_1 (
    .a(multiplexer_2_out), .b(multiplexer_3_out), .out(subtractor_1_out), .bin(ALU_q[7]),
    .bout(subtractor_1_bout));
  assign nand_1_out = ~(multiplexer_2_out & multiplexer_3_out);  // NAND_Gate nand_1, 8 bits wide
  Shifter #(.shift("lr")) shifter_1 (.in(multiplexer_2_out), .\dist (multiplexer_3_out[2:0]), .out(shifter_1_out));
  Decoder #(.select(3)) decoder_2 (
    .out1(PC_READ_A), .out2(MAR_READ), .out3(A_READ), .out4(B_READ), .out5(C_READ), .out6(ALU_READ),
    .out7(IN_READ), .sel(SEG_ADDR[2:0]), .en(and_10_out));  // open: out0
  and and_10 (and_10_out, READ_EN, not_3_out);
  and and_11 (and_11_out, or_6_out, READ_EN);
  Decoder #(.select(3)) decoder_3 (
    .out0(PC_WRITE_A), .out1(RAM_WRITE), .out2(MAR_WRITE), .out3(A_WRITE), .out4(B_WRITE), .out5(C_WRITE),
    .out6(ALU_WRITE), .out7(OUT_WRITE), .sel({SEG_SEL, SEG_ADDR[4:3]}), .en(and_11_out));
  // Probe on ALU_q[1:0]
  Multiplexer #(.enable("false"), .select(2), .width(8)) multiplexer_4 (
    .in0(adder_1_out), .in1(subtractor_1_out), .in2(nand_1_out), .in3(shifter_1_out),
    .out(multiplexer_4_out), .sel(ALU_q[1:0]));
  Multiplexer #(.enable("false"), .select(2)) multiplexer_5 (
    .in0(adder_1_cout), .in1(subtractor_1_bout), .out(nor_1_out[1]), .sel(ALU_q[1:0]));  // open: in2, in3
  nor nor_1 (nor_1_out[0], multiplexer_4_out[0], multiplexer_4_out[1], multiplexer_4_out[2], multiplexer_4_out[3], multiplexer_4_out[4], multiplexer_4_out[5], multiplexer_4_out[6], multiplexer_4_out[7]);
  Pull_Resistor pull_resistor_3 (.node(nor_1_out[1]));
  Register #(.trigger("high"), .width(2)) F (.D(nor_1_out), .en(ALU_WRITE), .clk(CLK), .Q({CARRY, ZERO}));  // open: clr

  // Other names for the same wires on the sheet: PC_READ_B = IR_WRITE; PC_SEL = IR_WRITE; PC_WRITE_B = PC_READ_C;
  //   WRITE_EN = READ_EN
endmodule
